# Fritzing sketch Untitled Sketch (saved by Fritzing 0.9.3b)

parts:
  WeMos_D1_Mini1 = WeMos D1 Mini
  config = Pushbutton [package="[THT]"]
  VCC1 = Battery
  sensor = Camdenboss CTB0158-2 [part_number=CTB0158-2 package=THT]
  part = Resistor [tolerance=±5% resistance=1k package=THT]

nets:
  N1: WeMos_D1_Mini1.3V3, VCC1.+
  N2: WeMos_D1_Mini1.D0, part.Pin_0
  N3: WeMos_D1_Mini1.D5, config.Pin_4
  N4: WeMos_D1_Mini1.D6, sensor.pin1
  N5: WeMos_D1_Mini1.G, config.Pin_1, config.Pin_2, VCC1.-, sensor.pin2
  N6: WeMos_D1_Mini1.RST, part.Pin_1
